# Fritzing sketch AlarmBoy (saved by Fritzing 0.9.3b)
breadboards: 2

parts:
  パーツ1 = Arduino Nano (Rev3.0)
  R1 = Resistor [tolerance=±5% resistance=1k package=THT]
  R2 = Resistor [tolerance=±5% resistance=1k package=THT]
  R3 = Resistor [tolerance=±5% resistance=1k package=THT]
  R4 = Resistor [tolerance=±5% resistance=1k package=THT]
  R5 = Resistor [tolerance=±5% resistance=1k package=THT]
  R6 = Resistor [tolerance=±5% resistance=1k package=THT]
  R7 = Resistor [tolerance=±5% resistance=1k package=THT]
  R8 = Resistor [tolerance=±5% resistance=1k package=THT]
  LED1 = LED - 3mm [color="Yellow (595nm)" package="3 mm [THT]"]
  LED2 = LED - 3mm [color="Red (660nm)" package="3 mm [THT]"]
  LED3 = LED - 3mm [color="Green (570nm)" package="3 mm [THT]"]
  LED4 = LED - 3mm [color="Blue (430nm)" package="3 mm [THT]"]
  J1 = Piezo Speaker
  S1 = Pushbutton [package="[THT]"]
  R9 = Resistor [tolerance=±5% resistance=82 package=THT]
  LED5 = LED - 3mm [color="Blue (430nm)" package="3 mm [THT]"]
  LED6 = LED - 3mm [color="Red (660nm)" package="3 mm [THT]"]

nets:
  N1: パーツ1.RESET, R9.Pin_0
  N2: パーツ1.GND, R1.Pin_0, R2.Pin_0, R3.Pin_0, R4.Pin_0, R5.Pin_0, R6.Pin_0, R7.Pin_0, R8.Pin_0, J1.pin1, S1.Pin_3, S1.Pin_4
  N3: パーツ1.D2, LED6.anode
  N4: パーツ1.D3, LED1.anode
  N5: パーツ1.D4, LED2.anode
  N6: パーツ1.D5, LED3.anode
  N7: パーツ1.D8, LED4.anode
  N8: パーツ1.D9, LED5.anode
  N9: パーツ1.5V, R9.Pin_1
  N10: パーツ1.A5, J1.pin2
  N11: パーツ1.A3, S1.Pin_2
  N12: R1.Pin_1, LED6.cathode
  N13: R2.Pin_1, LED1.cathode
  N14: R3.Pin_1, LED2.cathode
  N15: R4.Pin_1, LED3.cathode
  N16: R5.Pin_1, LED4.cathode
  N17: R8.Pin_1, LED5.cathode
